// Logisim project ALU_Andres_y_Daniel.circ as structural Verilog: 20 circuits, main circuit main
module main (
  input  [31:0] in_1,
  input  [31:0] in_2,
  input  [4:0] in_3,
  output out_4,
  output out_5,
  output [31:0] out_6
);

  ALU_32_bit alu_32_bit_1 (.A(in_1), .B(in_2), .op(in_3), .negative(out_4), .overflow(out_5), .out1(out_6));
endmodule

module ALU_32_bit (
  input  [31:0] A,
  input  [31:0] B,
  input  [4:0] op,
  output negative,
  output overflow,
  output [31:0] out1
);

  wire add_overflow, addi_overflow;
  wire [31:0] add_result, addi_result, and1_result, beq1_out_3, bgt1_gto, blt1_lto, bne1_out_3,
       divider_1_out, j_o, jal_o, jr_o, la_o, li_o, lw_o, mfhi_o, mflo_o, move_o, multiplier_1_out,
       or1_result, sll1_out_3, srl1_out_3, sub_result, sw_o;

  L_32_bit_Adder add (.A(A), .B(B), .overflow(add_overflow), .Result(add_result));
  L_32_bit_Subtractor sub (.A(A), .B(B), .negative(negative), .Result(sub_result));
  L_32_bit_Adder addi (.A(A), .B(B), .overflow(addi_overflow), .Result(addi_result));
  L_32_Pass mfhi (.a(A), .b(B), .o(mfhi_o));
  L_32_Pass mflo (.a(A), .b(B), .o(mflo_o));
  L_32_bit_AND and1 (.A(A), .B(B), .Result(and1_result));
  L_32_bit_OR or1 (.A(A), .B(B), .Result(or1_result));
  sllx sll1 (.in_1(A), .in_2(B), .out_3(sll1_out_3));
  srlx srl1 (.in_1(A), .in_2(B), .out_3(srl1_out_3));
  L_32_Pass j (.a(A), .b(B), .o(j_o));
  L_32_Pass jal (.a(A), .b(B), .o(jal_o));
  L_32_Pass jr (.a(A), .b(B), .o(jr_o));
  beq beq1 (.a(A), .b(B), .out_3(beq1_out_3));
  bne bne1 (.in_1(A), .in_2(B), .out_3(bne1_out_3));
  bgt bgt1 (.a(A), .b(B), .gto(bgt1_gto));
  blt blt1 (.a(A), .b(B), .lto(blt1_lto));
  L_32_Pass move (.a(A), .b(B), .o(move_o));
  L_32_Pass li (.a(A), .b(B), .o(li_o));
  L_32_Pass la (.a(A), .b(B), .o(la_o));
  L_32_Pass lw (.a(A), .b(B), .o(lw_o));
  L_32_Pass sw (.a(A), .b(B), .o(sw_o));
  Multiplier #(.width(32)) multiplier_1 (.a(A), .b(B), .out(multiplier_1_out));  // open: cin, cout
  Divider #(.width(32)) divider_1 (.a(A), .b(B), .out(divider_1_out));  // open: upper, rem
  or or_1 (overflow, add_overflow, addi_overflow);
  Multiplexer #(.enable("false"), .select(5), .width(32)) multiplexer_1 (
    .in0(add_result), .in1(sub_result), .in2(addi_result), .in3(multiplier_1_out), .in4(divider_1_out),
    .in5(mfhi_o), .in6(mflo_o), .in7(and1_result), .in8(or1_result), .in9(sll1_out_3), .in10(srl1_out_3),
    .in11(j_o), .in12(jal_o), .in13(jr_o), .in14(beq1_out_3), .in15(bne1_out_3), .in16(bgt1_gto),
    .in17(blt1_lto), .in18(move_o), .in19(li_o), .in20(la_o), .in21(lw_o), .in22(sw_o), .out(out1), .sel(op));  // open: in23, in24, in25, in26, in27, in28, in29, in30, in31
endmodule

// +
module L_1_bit_Adder (
  input  A,
  input  B,
  input  Carry_In,
  output Carry_Out,
  output Result
);

  wire and_1_out, and_2_out, xor_1_out;

  and and_1 (and_1_out, A, B);
  xor xor_1 (xor_1_out, A, B);
  or or_1 (Carry_Out, and_1_out, and_2_out);
  and and_2 (and_2_out, Carry_In, xor_1_out);
  xor xor_2 (Result, Carry_In, xor_1_out);

  // Notes on the sheet:
  //   Full Adder
endmodule

module L_4_bit_Adder (
  input  [3:0] A,
  input  [3:0] B,
  input  Carry_In,
  output Carry_Out,
  output [3:0] Result
);

  wire l_1_bit_adder_1_carry_out, l_1_bit_adder_2_carry_out, l_1_bit_adder_3_carry_out;

  L_1_bit_Adder l_1_bit_adder_1 (
    .A(A[0]), .B(B[0]), .Carry_Out(l_1_bit_adder_1_carry_out), .Carry_In(Carry_In), .Result(Result[0]));
  L_1_bit_Adder l_1_bit_adder_2 (
    .A(A[1]), .B(B[1]), .Carry_Out(l_1_bit_adder_2_carry_out), .Carry_In(l_1_bit_adder_1_carry_out),
    .Result(Result[1]));
  L_1_bit_Adder l_1_bit_adder_3 (
    .A(A[2]), .B(B[2]), .Carry_Out(l_1_bit_adder_3_carry_out), .Carry_In(l_1_bit_adder_2_carry_out),
    .Result(Result[2]));
  L_1_bit_Adder l_1_bit_adder_4 (
    .A(A[3]), .B(B[3]), .Carry_Out(Carry_Out), .Carry_In(l_1_bit_adder_3_carry_out), .Result(Result[3]));
endmodule

module L_16_bit_Adder (
  input  [15:0] A,
  input  [15:0] B,
  input  Carry_In,
  output Carry_Out,
  output [15:0] Result
);

  wire l_4_bit_adder_1_carry_out, l_4_bit_adder_2_carry_out, l_4_bit_adder_3_carry_out;

  L_4_bit_Adder l_4_bit_adder_1 (
    .Carry_In(Carry_In), .A(A[3:0]), .B(B[3:0]), .Result(Result[3:0]), .Carry_Out(l_4_bit_adder_1_carry_out));
  L_4_bit_Adder l_4_bit_adder_2 (
    .Carry_In(l_4_bit_adder_1_carry_out), .A(A[7:4]), .B(B[7:4]), .Result(Result[7:4]),
    .Carry_Out(l_4_bit_adder_2_carry_out));
  L_4_bit_Adder l_4_bit_adder_3 (
    .Carry_In(l_4_bit_adder_2_carry_out), .A(A[11:8]), .B(B[11:8]), .Result(Result[11:8]),
    .Carry_Out(l_4_bit_adder_3_carry_out));
  L_4_bit_Adder l_4_bit_adder_4 (
    .Carry_In(l_4_bit_adder_3_carry_out), .A(A[15:12]), .B(B[15:12]), .Result(Result[15:12]),
    .Carry_Out(Carry_Out));
endmodule

module L_32_bit_AND (
  input  [31:0] A,
  input  [31:0] B,
  output [31:0] Result
);

  assign Result = A & B;  // AND_Gate and_1, 32 bits wide

  // Notes on the sheet:
  //   32-bit AND
endmodule

module L_32_bit_OR (
  input  [31:0] A,
  input  [31:0] B,
  output [31:0] Result
);

  assign Result = A | B;  // OR_Gate or_1, 32 bits wide

  // Notes on the sheet:
  //   32-bit OR
endmodule

module L_32_bit_Adder_Subtracter (
  input  [31:0] A,
  input  [31:0] B,
  input  Carry_In,
  output Carry_Out,
  output [31:0] Result
);

  wire l_16_bit_adder_1_carry_out;
  wire [15:0] bit_extender_1_out, xor_1_out, xor_2_out;

  assign bit_extender_1_out = {{15{Carry_In}}, Carry_In};  // Bit_Extender bit_extender_1
  assign xor_1_out = bit_extender_1_out ^ B[15:0];  // XOR_Gate xor_1, 16 bits wide
  L_16_bit_Adder l_16_bit_adder_1 (
    .Carry_In(Carry_In), .A(A[15:0]), .B(xor_1_out), .Result(Result[15:0]),
    .Carry_Out(l_16_bit_adder_1_carry_out));
  assign xor_2_out = bit_extender_1_out ^ B[31:16];  // XOR_Gate xor_2, 16 bits wide
  L_16_bit_Adder l_16_bit_adder_2 (
    .Carry_In(l_16_bit_adder_1_carry_out), .A(A[31:16]), .B(xor_2_out), .Result(Result[31:16]),
    .Carry_Out(Carry_Out));

  // Notes on the sheet:
  //   32 bit Adder/Subtracter
endmodule

module L_32_bit_Subtractor (
  input  [31:0] A,
  input  [31:0] B,
  output negative,
  output [31:0] Result
);

  wire l_32_bit_adder_subtracter_1_carry_out;

  not not_1 (negative, l_32_bit_adder_subtracter_1_carry_out);
  L_32_bit_Adder_Subtracter l_32_bit_adder_subtracter_1 (
    .A(A), .B(B), .Carry_Out(l_32_bit_adder_subtracter_1_carry_out), .Carry_In(1'b1), .Result(Result));
endmodule

module L_32_bit_Adder (
  input  [31:0] A,
  input  [31:0] B,
  output overflow,
  output [31:0] Result
);

  L_32_bit_Adder_Subtracter l_32_bit_adder_subtracter_1 (
    .A(A), .B(B), .Carry_Out(overflow), .Result(Result));  // open: Carry_In
endmodule

module L_32_Pass (
  input  [31:0] a,
  input  [31:0] b,
  output [31:0] o
);


  assign o = a;
endmodule

module beq (
  input  [31:0] a,
  input  [31:0] b,
  output [31:0] out_3
);

  wire and_1_out;
  wire [31:0] xnor_1_out;

  assign xnor_1_out = ~(a ^ b);  // XNOR_Gate xnor_1, 32 bits wide
  and and_1 (and_1_out, xnor_1_out[0], xnor_1_out[1], xnor_1_out[2], xnor_1_out[3], xnor_1_out[4], xnor_1_out[5], xnor_1_out[6], xnor_1_out[7], xnor_1_out[8], xnor_1_out[9], xnor_1_out[10], xnor_1_out[11], xnor_1_out[12], xnor_1_out[13], xnor_1_out[14], xnor_1_out[15], xnor_1_out[17], xnor_1_out[18], xnor_1_out[19], xnor_1_out[20], xnor_1_out[21], xnor_1_out[22], xnor_1_out[23], xnor_1_out[24], xnor_1_out[25], xnor_1_out[26], xnor_1_out[27], xnor_1_out[28], xnor_1_out[29], xnor_1_out[30], xnor_1_out[31], xnor_1_out[16]);
  assign out_3 = {{31{and_1_out}}, and_1_out};  // Bit_Extender bit_extender_1
endmodule

module bne (
  input  [31:0] in_1,
  input  [31:0] in_2,
  output [31:0] out_3
);

  wire [31:0] beq_1_out_3;

  beq beq_1 (.a(in_1), .b(in_2), .out_3(beq_1_out_3));
  assign out_3 = ~beq_1_out_3;  // NOT_Gate not_1, 32 bits wide
endmodule

module comparator_4_bit (
  input  [3:0] a,
  input  [3:0] b,
  input  gti,
  input  eqi,
  input  lti,
  output gto,
  output eqo,
  output lto
);

  wire and_3_out, and_4_out, and_5_out, and_6_out, and_7_out, nand_1_out, or_1_out, or_2_out;
  wire [3:0] and_1_out, and_2_out, not_1_out, not_2_out, xnor_1_out;

  assign not_1_out = ~a;  // NOT_Gate not_1, 4 bits wide
  assign and_1_out = a & not_2_out;  // AND_Gate and_1, 4 bits wide
  assign not_2_out = ~b;  // NOT_Gate not_2, 4 bits wide
  assign xnor_1_out = ~(b ^ a);  // XNOR_Gate xnor_1, 4 bits wide
  assign and_2_out = not_1_out & b;  // AND_Gate and_2, 4 bits wide
  or or_1 (or_1_out, and_1_out[0], and_1_out[1], and_1_out[3], and_1_out[2]);
  and and_3 (and_3_out, xnor_1_out[0], xnor_1_out[1], xnor_1_out[3], xnor_1_out[2]);
  or or_2 (or_2_out, and_2_out[0], and_2_out[1], and_2_out[3], and_2_out[2]);
  and and_4 (and_4_out, gti, and_3_out);
  and and_5 (and_5_out, and_3_out, eqi);
  and and_6 (and_6_out, and_3_out, lti);
  or or_3 (gto, or_1_out, and_4_out);
  or or_4 (lto, and_6_out, or_2_out);
  nand nand_1 (nand_1_out, gti, eqi, lti);
  and and_7 (and_7_out, nand_1_out, and_3_out);
  or or_5 (eqo, and_5_out, and_7_out);
endmodule

module bgt (
  input  [31:0] a,
  input  [31:0] b,
  output [31:0] gto
);

  wire comparator_4_bit_1_eqo, comparator_4_bit_1_gto, comparator_4_bit_1_lto, comparator_4_bit_2_eqo,
       comparator_4_bit_2_gto, comparator_4_bit_2_lto, comparator_4_bit_3_eqo, comparator_4_bit_3_gto,
       comparator_4_bit_3_lto, comparator_4_bit_4_eqo, comparator_4_bit_4_gto, comparator_4_bit_4_lto,
       comparator_4_bit_5_eqo, comparator_4_bit_5_gto, comparator_4_bit_5_lto, comparator_4_bit_6_eqo,
       comparator_4_bit_6_gto, comparator_4_bit_6_lto, comparator_4_bit_7_eqo, comparator_4_bit_7_gto,
       comparator_4_bit_7_lto, comparator_4_bit_8_eqo, comparator_4_bit_8_gto, comparator_4_bit_8_lto;

  comparator_4_bit comparator_4_bit_1 (
    .a(a[3:0]), .b(b[3:0]), .gto(comparator_4_bit_1_gto), .eqo(comparator_4_bit_1_eqo),
    .lto(comparator_4_bit_1_lto));  // open: gti, eqi, lti
  comparator_4_bit comparator_4_bit_2 (
    .a(a[7:4]), .b(b[7:4]), .gti(comparator_4_bit_1_gto), .eqi(comparator_4_bit_1_eqo),
    .lti(comparator_4_bit_1_lto), .gto(comparator_4_bit_2_gto), .eqo(comparator_4_bit_2_eqo),
    .lto(comparator_4_bit_2_lto));
  comparator_4_bit comparator_4_bit_3 (
    .a(a[11:8]), .b(b[11:8]), .gti(comparator_4_bit_2_gto), .eqi(comparator_4_bit_2_eqo),
    .lti(comparator_4_bit_2_lto), .gto(comparator_4_bit_3_gto), .eqo(comparator_4_bit_3_eqo),
    .lto(comparator_4_bit_3_lto));
  comparator_4_bit comparator_4_bit_4 (
    .a(a[15:12]), .b(b[15:12]), .gti(comparator_4_bit_3_gto), .eqi(comparator_4_bit_3_eqo),
    .lti(comparator_4_bit_3_lto), .gto(comparator_4_bit_4_gto), .eqo(comparator_4_bit_4_eqo),
    .lto(comparator_4_bit_4_lto));
  comparator_4_bit comparator_4_bit_5 (
    .a(a[19:16]), .b(b[19:16]), .gti(comparator_4_bit_4_gto), .eqi(comparator_4_bit_4_eqo),
    .lti(comparator_4_bit_4_lto), .gto(comparator_4_bit_5_gto), .eqo(comparator_4_bit_5_eqo),
    .lto(comparator_4_bit_5_lto));
  comparator_4_bit comparator_4_bit_6 (
    .a(a[23:20]), .b(b[23:20]), .gti(comparator_4_bit_5_gto), .eqi(comparator_4_bit_5_eqo),
    .lti(comparator_4_bit_5_lto), .gto(comparator_4_bit_6_gto), .eqo(comparator_4_bit_6_eqo),
    .lto(comparator_4_bit_6_lto));
  comparator_4_bit comparator_4_bit_7 (
    .a(a[27:24]), .b(b[27:24]), .gti(comparator_4_bit_6_gto), .eqi(comparator_4_bit_6_eqo),
    .lti(comparator_4_bit_6_lto), .gto(comparator_4_bit_7_gto), .eqo(comparator_4_bit_7_eqo),
    .lto(comparator_4_bit_7_lto));
  comparator_4_bit comparator_4_bit_8 (
    .a(a[31:28]), .b(b[31:28]), .gti(comparator_4_bit_7_gto), .eqi(comparator_4_bit_7_eqo),
    .lti(comparator_4_bit_7_lto), .gto(comparator_4_bit_8_gto), .eqo(comparator_4_bit_8_eqo),
    .lto(comparator_4_bit_8_lto));
  assign gto = {{31{comparator_4_bit_8_gto}}, comparator_4_bit_8_gto};  // Bit_Extender bit_extender_1
endmodule

module blt (
  input  [31:0] a,
  input  [31:0] b,
  output [31:0] lto
);

  wire comparator_4_bit_1_eqo, comparator_4_bit_1_gto, comparator_4_bit_1_lto, comparator_4_bit_2_eqo,
       comparator_4_bit_2_gto, comparator_4_bit_2_lto, comparator_4_bit_3_eqo, comparator_4_bit_3_gto,
       comparator_4_bit_3_lto, comparator_4_bit_4_eqo, comparator_4_bit_4_gto, comparator_4_bit_4_lto,
       comparator_4_bit_5_eqo, comparator_4_bit_5_gto, comparator_4_bit_5_lto, comparator_4_bit_6_eqo,
       comparator_4_bit_6_gto, comparator_4_bit_6_lto, comparator_4_bit_7_eqo, comparator_4_bit_7_gto,
       comparator_4_bit_7_lto, comparator_4_bit_8_eqo, comparator_4_bit_8_gto, comparator_4_bit_8_lto;

  comparator_4_bit comparator_4_bit_1 (
    .a(a[3:0]), .b(b[3:0]), .gto(comparator_4_bit_1_gto), .eqo(comparator_4_bit_1_eqo),
    .lto(comparator_4_bit_1_lto));  // open: gti, eqi, lti
  comparator_4_bit comparator_4_bit_2 (
    .a(a[7:4]), .b(b[7:4]), .gti(comparator_4_bit_1_gto), .eqi(comparator_4_bit_1_eqo),
    .lti(comparator_4_bit_1_lto), .gto(comparator_4_bit_2_gto), .eqo(comparator_4_bit_2_eqo),
    .lto(comparator_4_bit_2_lto));
  comparator_4_bit comparator_4_bit_3 (
    .a(a[11:8]), .b(b[11:8]), .gti(comparator_4_bit_2_gto), .eqi(comparator_4_bit_2_eqo),
    .lti(comparator_4_bit_2_lto), .gto(comparator_4_bit_3_gto), .eqo(comparator_4_bit_3_eqo),
    .lto(comparator_4_bit_3_lto));
  comparator_4_bit comparator_4_bit_4 (
    .a(a[15:12]), .b(b[15:12]), .gti(comparator_4_bit_3_gto), .eqi(comparator_4_bit_3_eqo),
    .lti(comparator_4_bit_3_lto), .gto(comparator_4_bit_4_gto), .eqo(comparator_4_bit_4_eqo),
    .lto(comparator_4_bit_4_lto));
  comparator_4_bit comparator_4_bit_5 (
    .a(a[19:16]), .b(b[19:16]), .gti(comparator_4_bit_4_gto), .eqi(comparator_4_bit_4_eqo),
    .lti(comparator_4_bit_4_lto), .gto(comparator_4_bit_5_gto), .eqo(comparator_4_bit_5_eqo),
    .lto(comparator_4_bit_5_lto));
  comparator_4_bit comparator_4_bit_6 (
    .a(a[23:20]), .b(b[23:20]), .gti(comparator_4_bit_5_gto), .eqi(comparator_4_bit_5_eqo),
    .lti(comparator_4_bit_5_lto), .gto(comparator_4_bit_6_gto), .eqo(comparator_4_bit_6_eqo),
    .lto(comparator_4_bit_6_lto));
  comparator_4_bit comparator_4_bit_7 (
    .a(a[27:24]), .b(b[27:24]), .gti(comparator_4_bit_6_gto), .eqi(comparator_4_bit_6_eqo),
    .lti(comparator_4_bit_6_lto), .gto(comparator_4_bit_7_gto), .eqo(comparator_4_bit_7_eqo),
    .lto(comparator_4_bit_7_lto));
  comparator_4_bit comparator_4_bit_8 (
    .a(a[31:28]), .b(b[31:28]), .gti(comparator_4_bit_7_gto), .eqi(comparator_4_bit_7_eqo),
    .lti(comparator_4_bit_7_lto), .gto(comparator_4_bit_8_gto), .eqo(comparator_4_bit_8_eqo),
    .lto(comparator_4_bit_8_lto));
  assign lto = {{31{comparator_4_bit_8_lto}}, comparator_4_bit_8_lto};  // Bit_Extender bit_extender_1
endmodule

module L_32_bit_SRL (
  input  [31:0] in_1,
  output [31:0] out_2
);

  wire and_1_out, and_3_out, and_4_out, and_5_out, and_6_out, and_7_out, and_8_out, and_9_out, and_10_out,
       and_11_out, and_12_out, and_13_out, and_14_out, and_15_out, and_16_out, and_17_out, and_18_out,
       and_19_out, and_20_out, and_21_out, and_22_out, and_23_out, and_24_out, and_25_out, and_26_out,
       and_27_out, and_28_out, and_29_out, and_30_out, and_31_out, and_32_out, and_33_out, and_34_out,
       and_35_out, and_36_out, and_37_out, and_38_out, and_39_out, and_40_out, and_41_out, and_42_out,
       and_43_out, and_44_out, and_45_out, and_46_out, and_47_out, and_48_out, and_49_out, and_50_out,
       and_51_out, and_52_out, and_53_out, and_54_out, and_55_out, and_56_out, and_57_out, and_58_out,
       and_59_out, and_60_out, and_62_out, not_1_out;

  not not_1 (not_1_out, 1'b1);
  and and_1 (and_1_out, in_1[0], 1'b1);
  and and_2 (out_2[0], not_1_out, in_1[1]);
  or or_1 (out_2[1], and_1_out, and_4_out);
  and and_3 (and_3_out, in_1[1], 1'b1);
  and and_4 (and_4_out, not_1_out, in_1[2]);
  and and_5 (and_5_out, in_1[2], 1'b1);
  or or_2 (out_2[2], and_3_out, and_6_out);
  and and_6 (and_6_out, not_1_out, in_1[3]);
  and and_7 (and_7_out, in_1[3], 1'b1);
  or or_3 (out_2[3], and_5_out, and_8_out);
  and and_8 (and_8_out, not_1_out, in_1[4]);
  or or_4 (out_2[4], and_7_out, and_10_out);
  and and_9 (and_9_out, in_1[4], 1'b1);
  and and_10 (and_10_out, not_1_out, in_1[5]);
  or or_5 (out_2[5], and_9_out, and_12_out);
  and and_11 (and_11_out, in_1[5], 1'b1);
  and and_12 (and_12_out, not_1_out, in_1[6]);
  and and_13 (and_13_out, in_1[6], 1'b1);
  or or_6 (out_2[6], and_11_out, and_14_out);
  and and_14 (and_14_out, not_1_out, in_1[7]);
  or or_7 (out_2[7], and_13_out, and_16_out);
  and and_15 (and_15_out, in_1[7], 1'b1);
  and and_16 (and_16_out, not_1_out, in_1[8]);
  or or_8 (out_2[8], and_15_out, and_18_out);
  and and_17 (and_17_out, in_1[8], 1'b1);
  and and_18 (and_18_out, not_1_out, in_1[9]);
  and and_19 (and_19_out, in_1[9], 1'b1);
  or or_9 (out_2[9], and_17_out, and_20_out);
  and and_20 (and_20_out, not_1_out, in_1[10]);
  or or_10 (out_2[10], and_19_out, and_22_out);
  and and_21 (and_21_out, in_1[10], 1'b1);
  and and_22 (and_22_out, not_1_out, in_1[11]);
  or or_11 (out_2[11], and_21_out, and_24_out);
  and and_23 (and_23_out, in_1[11], 1'b1);
  and and_24 (and_24_out, not_1_out, in_1[12]);
  and and_25 (and_25_out, in_1[12], 1'b1);
  or or_12 (out_2[12], and_23_out, and_26_out);
  and and_26 (and_26_out, not_1_out, in_1[13]);
  or or_13 (out_2[13], and_25_out, and_28_out);
  and and_27 (and_27_out, in_1[13], 1'b1);
  and and_28 (and_28_out, not_1_out, in_1[14]);
  or or_14 (out_2[14], and_27_out, and_30_out);
  and and_29 (and_29_out, in_1[14], 1'b1);
  and and_30 (and_30_out, not_1_out, in_1[15]);
  and and_31 (and_31_out, in_1[15], 1'b1);
  or or_15 (out_2[15], and_29_out, and_32_out);
  and and_32 (and_32_out, not_1_out, in_1[16]);
  and and_33 (and_33_out, in_1[16], 1'b1);
  or or_16 (out_2[16], and_31_out, and_34_out);
  and and_34 (and_34_out, not_1_out, in_1[17]);
  or or_17 (out_2[17], and_33_out, and_36_out);
  and and_35 (and_35_out, in_1[17], 1'b1);
  and and_36 (and_36_out, not_1_out, in_1[18]);
  and and_37 (and_37_out, in_1[18], 1'b1);
  or or_18 (out_2[18], and_35_out, and_38_out);
  and and_38 (and_38_out, not_1_out, in_1[19]);
  and and_39 (and_39_out, in_1[19], 1'b1);
  or or_19 (out_2[19], and_37_out, and_40_out);
  and and_40 (and_40_out, not_1_out, in_1[20]);
  or or_20 (out_2[20], and_39_out, and_42_out);
  and and_41 (and_41_out, in_1[20], 1'b1);
  and and_42 (and_42_out, not_1_out, in_1[21]);
  and and_43 (and_43_out, in_1[21], 1'b1);
  or or_21 (out_2[21], and_41_out, and_44_out);
  and and_44 (and_44_out, not_1_out, in_1[22]);
  and and_45 (and_45_out, in_1[22], 1'b1);
  or or_22 (out_2[22], and_43_out, and_46_out);
  and and_46 (and_46_out, not_1_out, in_1[23]);
  or or_23 (out_2[23], and_45_out, and_48_out);
  and and_47 (and_47_out, in_1[23], 1'b1);
  and and_48 (and_48_out, not_1_out, in_1[24]);
  or or_24 (out_2[24], and_47_out, and_50_out);
  and and_49 (and_49_out, in_1[24], 1'b1);
  and and_50 (and_50_out, not_1_out, in_1[25]);
  and and_51 (and_51_out, in_1[25], 1'b1);
  or or_25 (out_2[25], and_49_out, and_52_out);
  and and_52 (and_52_out, not_1_out, in_1[26]);
  or or_26 (out_2[26], and_51_out, and_54_out);
  and and_53 (and_53_out, in_1[26], 1'b1);
  and and_54 (and_54_out, not_1_out, in_1[27]);
  or or_27 (out_2[27], and_53_out, and_56_out);
  and and_55 (and_55_out, in_1[27], 1'b1);
  and and_56 (and_56_out, not_1_out, in_1[28]);
  and and_57 (and_57_out, in_1[28], 1'b1);
  or or_28 (out_2[28], and_55_out, and_58_out);
  and and_58 (and_58_out, not_1_out, in_1[29]);
  and and_59 (and_59_out, in_1[29], 1'b1);
  or or_29 (out_2[29], and_57_out, and_60_out);
  and and_60 (and_60_out, not_1_out, in_1[30]);
  or or_30 (out_2[30], and_59_out, and_62_out);
  and and_61 (out_2[31], in_1[30], 1'b1);
  and and_62 (and_62_out, not_1_out, in_1[31]);
endmodule

module L_32_bit_SLL (
  input  [31:0] in_1,
  output [31:0] out_2
);

  wire and_1_out, and_3_out, and_4_out, and_5_out, and_6_out, and_7_out, and_8_out, and_9_out, and_10_out,
       and_11_out, and_12_out, and_13_out, and_14_out, and_15_out, and_16_out, and_17_out, and_18_out,
       and_19_out, and_20_out, and_21_out, and_22_out, and_23_out, and_24_out, and_25_out, and_26_out,
       and_27_out, and_28_out, and_29_out, and_30_out, and_31_out, and_32_out, and_33_out, and_34_out,
       and_35_out, and_36_out, and_37_out, and_38_out, and_39_out, and_40_out, and_41_out, and_42_out,
       and_43_out, and_44_out, and_45_out, and_46_out, and_47_out, and_48_out, and_49_out, and_50_out,
       and_51_out, and_52_out, and_53_out, and_54_out, and_55_out, and_56_out, and_57_out, and_58_out,
       and_59_out, and_60_out, and_62_out, not_1_out;

  not not_1 (not_1_out, 1'b0);
  and and_1 (and_1_out, in_1[0], 1'b0);
  and and_2 (out_2[0], not_1_out, in_1[1]);
  or or_1 (out_2[1], and_1_out, and_4_out);
  and and_3 (and_3_out, in_1[1], 1'b0);
  and and_4 (and_4_out, not_1_out, in_1[2]);
  and and_5 (and_5_out, in_1[2], 1'b0);
  or or_2 (out_2[2], and_3_out, and_6_out);
  and and_6 (and_6_out, not_1_out, in_1[3]);
  and and_7 (and_7_out, in_1[3], 1'b0);
  or or_3 (out_2[3], and_5_out, and_8_out);
  and and_8 (and_8_out, not_1_out, in_1[4]);
  or or_4 (out_2[4], and_7_out, and_10_out);
  and and_9 (and_9_out, in_1[4], 1'b0);
  and and_10 (and_10_out, not_1_out, in_1[5]);
  or or_5 (out_2[5], and_9_out, and_12_out);
  and and_11 (and_11_out, in_1[5], 1'b0);
  and and_12 (and_12_out, not_1_out, in_1[6]);
  and and_13 (and_13_out, in_1[6], 1'b0);
  or or_6 (out_2[6], and_11_out, and_14_out);
  and and_14 (and_14_out, not_1_out, in_1[7]);
  or or_7 (out_2[7], and_13_out, and_16_out);
  and and_15 (and_15_out, in_1[7], 1'b0);
  and and_16 (and_16_out, not_1_out, in_1[8]);
  or or_8 (out_2[8], and_15_out, and_18_out);
  and and_17 (and_17_out, in_1[8], 1'b0);
  and and_18 (and_18_out, not_1_out, in_1[9]);
  and and_19 (and_19_out, in_1[9], 1'b0);
  or or_9 (out_2[9], and_17_out, and_20_out);
  and and_20 (and_20_out, not_1_out, in_1[10]);
  or or_10 (out_2[10], and_19_out, and_22_out);
  and and_21 (and_21_out, in_1[10], 1'b0);
  and and_22 (and_22_out, not_1_out, in_1[11]);
  or or_11 (out_2[11], and_21_out, and_24_out);
  and and_23 (and_23_out, in_1[11], 1'b0);
  and and_24 (and_24_out, not_1_out, in_1[12]);
  and and_25 (and_25_out, in_1[12], 1'b0);
  or or_12 (out_2[12], and_23_out, and_26_out);
  and and_26 (and_26_out, not_1_out, in_1[13]);
  or or_13 (out_2[13], and_25_out, and_28_out);
  and and_27 (and_27_out, in_1[13], 1'b0);
  and and_28 (and_28_out, not_1_out, in_1[14]);
  or or_14 (out_2[14], and_27_out, and_30_out);
  and and_29 (and_29_out, in_1[14], 1'b0);
  and and_30 (and_30_out, not_1_out, in_1[15]);
  and and_31 (and_31_out, in_1[15], 1'b0);
  or or_15 (out_2[15], and_29_out, and_32_out);
  and and_32 (and_32_out, not_1_out, in_1[16]);
  and and_33 (and_33_out, in_1[16], 1'b0);
  or or_16 (out_2[16], and_31_out, and_34_out);
  and and_34 (and_34_out, not_1_out, in_1[17]);
  or or_17 (out_2[17], and_33_out, and_36_out);
  and and_35 (and_35_out, in_1[17], 1'b0);
  and and_36 (and_36_out, not_1_out, in_1[18]);
  and and_37 (and_37_out, in_1[18], 1'b0);
  or or_18 (out_2[18], and_35_out, and_38_out);
  and and_38 (and_38_out, not_1_out, in_1[19]);
  and and_39 (and_39_out, in_1[19], 1'b0);
  or or_19 (out_2[19], and_37_out, and_40_out);
  and and_40 (and_40_out, not_1_out, in_1[20]);
  or or_20 (out_2[20], and_39_out, and_42_out);
  and and_41 (and_41_out, in_1[20], 1'b0);
  and and_42 (and_42_out, not_1_out, in_1[21]);
  and and_43 (and_43_out, in_1[21], 1'b0);
  or or_21 (out_2[21], and_41_out, and_44_out);
  and and_44 (and_44_out, not_1_out, in_1[22]);
  and and_45 (and_45_out, in_1[22], 1'b0);
  or or_22 (out_2[22], and_43_out, and_46_out);
  and and_46 (and_46_out, not_1_out, in_1[23]);
  or or_23 (out_2[23], and_45_out, and_48_out);
  and and_47 (and_47_out, in_1[23], 1'b0);
  and and_48 (and_48_out, not_1_out, in_1[24]);
  or or_24 (out_2[24], and_47_out, and_50_out);
  and and_49 (and_49_out, in_1[24], 1'b0);
  and and_50 (and_50_out, not_1_out, in_1[25]);
  and and_51 (and_51_out, in_1[25], 1'b0);
  or or_25 (out_2[25], and_49_out, and_52_out);
  and and_52 (and_52_out, not_1_out, in_1[26]);
  or or_26 (out_2[26], and_51_out, and_54_out);
  and and_53 (and_53_out, in_1[26], 1'b0);
  and and_54 (and_54_out, not_1_out, in_1[27]);
  or or_27 (out_2[27], and_53_out, and_56_out);
  and and_55 (and_55_out, in_1[27], 1'b0);
  and and_56 (and_56_out, not_1_out, in_1[28]);
  and and_57 (and_57_out, in_1[28], 1'b0);
  or or_28 (out_2[28], and_55_out, and_58_out);
  and and_58 (and_58_out, not_1_out, in_1[29]);
  and and_59 (and_59_out, in_1[29], 1'b0);
  or or_29 (out_2[29], and_57_out, and_60_out);
  and and_60 (and_60_out, not_1_out, in_1[30]);
  or or_30 (out_2[30], and_59_out, and_62_out);
  and and_61 (out_2[31], in_1[30], 1'b0);
  and and_62 (and_62_out, not_1_out, in_1[31]);
endmodule

module sllx (
  input  [31:0] in_1,
  input  [31:0] in_2,
  output [31:0] out_3
);

  Shifter #(.width(32)) shifter_1 (.in(in_1), .\dist (in_2[4:0]), .out(out_3));
endmodule

module srlx (
  input  [31:0] in_1,
  input  [31:0] in_2,
  output [31:0] out_3
);

  Shifter #(.shift("lr"), .width(32)) shifter_1 (.in(in_1), .\dist (in_2[4:0]), .out(out_3));
endmodule
